// Logisim project 1-6 UP Counter.circ as structural Verilog: 1 circuit, main circuit main
module main (
  input  in_1,
  output Q0,
  output Q1,
  output Q2
);

  wire and_1_out, clock_1_out, j_k_ff_1_qn, j_k_ff_2_qn;

  Clock clock_1 (.out(clock_1_out));
  J_K_Flip_Flop j_k_ff_1 (
    .J(in_1), .clk(clock_1_out), .K(in_1), .Q(Q0), .Qn(j_k_ff_1_qn), .preset(and_1_out));  // open: en, reset
  J_K_Flip_Flop j_k_ff_2 (
    .J(in_1), .clk(j_k_ff_1_qn), .K(in_1), .Q(Q1), .Qn(j_k_ff_2_qn), .reset(and_1_out));  // open: preset, en
  and and_1 (and_1_out, Q0, Q1, Q2);
  J_K_Flip_Flop j_k_ff_3 (.J(in_1), .clk(j_k_ff_2_qn), .K(in_1), .Q(Q2), .reset(and_1_out));  // open: Qn, preset, en

  // Notes on the sheet:
  //   Clock
  //   1-6 UP Counter
endmodule
