// Logisim project 1-bit Adder with Carry using MUX.circ as structural Verilog: 1 circuit, main circuit main
module main (
  input  C_in,
  input  A,
  input  B,
  input  in_4,
  output Sum,
  output Carry
);

  wire not_1_out, not_2_out, not_3_out;

  not not_1 (not_1_out, C_in);
  not not_2 (not_2_out, C_in);
  Multiplexer #(.select(2)) multiplexer_1 (
    .in0(C_in), .in1(not_1_out), .in2(not_2_out), .in3(C_in), .out(Sum), .sel({B, A}));  // open: en
  Multiplexer #(.select(2)) multiplexer_2 (
    .in0(in_4), .in1(C_in), .in2(C_in), .in3(not_3_out), .out(Carry), .sel({B, A}));  // open: en
  not not_3 (not_3_out, in_4);

  // Notes on the sheet:
  //   Full Adder Circuit using MUX
endmodule
