// Logisim project 1-bit comparator.circ as structural Verilog: 1 circuit, main circuit main
module main (
  input  A,
  input  B
);

  wire and_1_out, and_2_out, not_1_out, not_2_out, xnor_1_out;

  not not_1 (not_1_out, B);
  not not_2 (not_2_out, A);
  xnor xnor_1 (xnor_1_out, A, B);
  and and_1 (and_1_out, A, not_1_out);
  and and_2 (and_2_out, B, not_2_out);
  LED led_1 (.in(xnor_1_out));
  LED led_2 (.in(and_1_out));
  LED led_3 (.in(and_2_out));

  // Notes on the sheet:
  //   1-bit Magnitude Comparator
  //   A=B
  //   A>B
  //   A<B
endmodule
