// Logisim project 3-bit Sychronous DOWN Counter using T Latch.circ as structural Verilog: 1 circuit, main circuit main
module main (
  input  CLK,
  output Q0,
  output Q1,
  output Q2
);

  wire and_1_out, clock_1_out, t_ff_1_qn, t_ff_2_qn;

  Clock clock_1 (.out(clock_1_out));
  T_Flip_Flop t_ff_1 (.clk(clock_1_out), .T(CLK), .Q(Q0), .Qn(t_ff_1_qn));  // open: preset, reset, en
  T_Flip_Flop t_ff_2 (.clk(clock_1_out), .T(t_ff_1_qn), .Q(Q1), .Qn(t_ff_2_qn));  // open: preset, reset, en
  and and_1 (and_1_out, t_ff_1_qn, t_ff_2_qn);
  T_Flip_Flop t_ff_3 (.clk(clock_1_out), .T(and_1_out), .Q(Q2));  // open: Qn, preset, reset, en

  // Notes on the sheet:
  //   3-bit Synchronous DOWN Counter
endmodule
