// Logisim project 3-bit Synchronous UP Counter using T Latch.circ as structural Verilog: 1 circuit, main circuit main
module main (
  input  CLK,
  output Q0,
  output Q1,
  output Q2
);

  wire and_1_out, clock_1_out;

  Clock clock_1 (.out(clock_1_out));
  T_Flip_Flop t_ff_1 (.clk(clock_1_out), .T(CLK), .Q(Q0));  // open: Qn, preset, reset, en
  T_Flip_Flop t_ff_2 (.clk(clock_1_out), .T(Q0), .Q(Q1));  // open: Qn, preset, reset, en
  and and_1 (and_1_out, Q0, Q1);
  T_Flip_Flop t_ff_3 (.clk(clock_1_out), .T(and_1_out), .Q(Q2));  // open: Qn, preset, reset, en

  // Notes on the sheet:
  //   3-bit Synchronous UP Counter
endmodule
