// Logisim project 4-Bit Adder,Subtractor.circ as structural Verilog
module Adder (
  input  A,
  input  B,
  input  Cin,
  output SUM,
  output CARRY
);

  wire and_1_out, and_2_out, and_3_out, and_4_out, and_5_out, and_6_out, and_7_out, and_8_out, and_9_out,
       and_10_out, and_11_out, not_1_out, not_2_out, not_3_out, not_4_out, not_5_out, not_6_out, or_1_out,
       or_3_out, or_4_out;

  not not_1 (not_1_out, A);
  not not_2 (not_2_out, B);
  not not_3 (not_3_out, A);
  not not_4 (not_4_out, B);
  and and_1 (and_1_out, B, Cin);
  and and_2 (and_2_out, A, Cin);
  and and_3 (and_3_out, not_1_out, not_2_out);
  and and_4 (and_4_out, not_3_out, B);
  not not_5 (not_5_out, Cin);
  and and_5 (and_5_out, A, not_4_out);
  not not_6 (not_6_out, Cin);
  and and_6 (and_6_out, A, B);
  or or_1 (or_1_out, and_1_out, and_2_out);
  and and_7 (and_7_out, A, B);
  and and_8 (and_8_out, and_3_out, Cin);
  and and_9 (and_9_out, and_4_out, not_5_out);
  and and_10 (and_10_out, and_5_out, not_6_out);
  and and_11 (and_11_out, and_6_out, Cin);
  or or_2 (CARRY, or_1_out, and_7_out);
  or or_3 (or_3_out, and_8_out, and_9_out);
  or or_4 (or_4_out, and_10_out, and_11_out);
  or or_5 (SUM, or_3_out, or_4_out);
endmodule

module _4_bit_adder (
  input  C_in,
  input  [3:0] A,
  input  [3:0] B,
  output [3:0] out_4,
  output C_out
);

  wire adder_1_carry, adder_2_carry, adder_3_carry, xor_1_out, xor_2_out, xor_3_out, xor_4_out;

  xor xor_1 (xor_1_out, B[0], C_in);
  xor xor_2 (xor_2_out, B[1], C_in);
  xor xor_3 (xor_3_out, B[2], C_in);
  xor xor_4 (xor_4_out, B[3], C_in);
  Adder adder_1 (.A(A[0]), .B(xor_1_out), .Cin(C_in), .SUM(out_4[0]), .CARRY(adder_1_carry));
  Adder adder_2 (.A(A[1]), .B(xor_2_out), .Cin(adder_1_carry), .SUM(out_4[1]), .CARRY(adder_2_carry));
  Adder adder_3 (.A(A[2]), .B(xor_3_out), .Cin(adder_2_carry), .SUM(out_4[2]), .CARRY(adder_3_carry));
  Adder adder_4 (.A(A[3]), .B(xor_4_out), .Cin(adder_3_carry), .SUM(out_4[3]), .CARRY(C_out));

  // Notes on the sheet:
  //   Sum Or Difference
endmodule
