// Logisim project 4-bit Johnson Counter using D Flipflop.circ as structural Verilog: 1 circuit, main circuit main
module main (
  input  in_1,
  output Q0,
  output Q1,
  output Q2,
  output Q3
);

  wire clock_1_out, d_ff_4_qn;

  Clock clock_1 (.out(clock_1_out));
  D_Flip_Flop d_ff_1 (.clk(clock_1_out), .D(d_ff_4_qn), .Q(Q0), .reset(in_1));  // open: Qn, preset, en
  D_Flip_Flop d_ff_2 (.clk(clock_1_out), .D(Q0), .Q(Q1), .reset(in_1));  // open: Qn, preset, en
  D_Flip_Flop d_ff_3 (.clk(clock_1_out), .D(Q1), .Q(Q2), .reset(in_1));  // open: Qn, preset, en
  D_Flip_Flop d_ff_4 (.clk(clock_1_out), .D(Q2), .Q(Q3), .Qn(d_ff_4_qn), .reset(in_1));  // open: preset, en

  // Notes on the sheet:
  //   CLK
  //   4-bit Johnson Counter using D FF
endmodule
