// Logisim project 4-bit Ring Counter using D Flipflop.circ as structural Verilog: 1 circuit, main circuit main
module main (
  input  Over_write,
  output Q0,
  output Q1,
  output Q2,
  output Q3
);

  wire clock_1_out;

  Clock clock_1 (.out(clock_1_out));
  D_Flip_Flop d_ff_1 (.clk(clock_1_out), .D(Q3), .Q(Q0), .preset(Over_write), .reset(Over_write));  // open: Qn, en
  D_Flip_Flop d_ff_2 (.clk(clock_1_out), .D(Q0), .Q(Q1), .reset(Over_write));  // open: Qn, preset, en
  D_Flip_Flop d_ff_3 (.clk(clock_1_out), .D(Q1), .Q(Q2), .reset(Over_write));  // open: Qn, preset, en
  D_Flip_Flop d_ff_4 (.clk(clock_1_out), .D(Q2), .Q(Q3), .reset(Over_write));  // open: Qn, preset, en

  // Notes on the sheet:
  //   CLK
  //   4-bit Ring Counter using D FF
endmodule
