// Logisim project 5-2 DOWN Counter.circ as structural Verilog: 1 circuit, main circuit main
module main (
  input  in_1,
  output Q0,
  output Q1,
  output Q2
);

  wire and_1_out, clock_1_out, j_k_ff_2_qn, j_k_ff_3_qn;

  Clock clock_1 (.out(clock_1_out));
  J_K_Flip_Flop j_k_ff_1 (.J(in_1), .clk(clock_1_out), .K(in_1), .Q(Q0), .preset(and_1_out));  // open: Qn, en, reset
  J_K_Flip_Flop j_k_ff_2 (
    .J(in_1), .clk(Q0), .K(in_1), .Q(Q1), .Qn(j_k_ff_2_qn), .reset(and_1_out));  // open: preset, en
  and and_1 (and_1_out, Q0, j_k_ff_2_qn, j_k_ff_3_qn);
  J_K_Flip_Flop j_k_ff_3 (
    .J(in_1), .clk(Q1), .K(in_1), .Q(Q2), .Qn(j_k_ff_3_qn), .preset(and_1_out));  // open: en, reset

  // Notes on the sheet:
  //   Clock
  //   5-2 DOWN Counter
endmodule
