// Logisim project AND Gate using MUX.circ as structural Verilog
module main (
  input  _0,
  input  B,
  input  Enabler,
  input  A,
  output A_B
);

  Multiplexer multiplexer_1 (.in0(_0), .in1(B), .out(A_B), .sel(A), .en(Enabler));

  // Notes on the sheet:
  //   AND Circuit
endmodule

module ANDmux (
  input  B,
  input  _1,
  input  Enabler,
  input  A,
  output A_B
);

  Multiplexer multiplexer_1 (.in0(B), .in1(_1), .out(A_B), .sel(A), .en(Enabler));

  // Notes on the sheet:
  //   A+B Circuit
endmodule

module ORmux (
  input  B,
  input  _0,
  input  Enabler,
  input  A,
  output A_prime_B
);

  Multiplexer multiplexer_1 (.in0(B), .in1(_0), .out(A_prime_B), .sel(A), .en(Enabler));

  // Notes on the sheet:
  //   A'.B Circuit
endmodule

module A_Bmux (
  input  _1,
  input  B,
  input  Enabler,
  input  A,
  output A_prime_B
);

  Multiplexer multiplexer_1 (.in0(_1), .in1(B), .out(A_prime_B), .sel(A), .en(Enabler));

  // Notes on the sheet:
  //   A'+B Circuit
endmodule

module A__Bmux (
  input  _0,
  input  in_2,
  input  A,
  input  _1,
  input  B,
  input  _0_2,
  input  Enable,
  input  _1_2,
  input  F2,
  input  F1,
  input  F0,
  input  C,
  output Y0,
  output Y1
);

  wire multiplexer_1_out, multiplexer_2_out, multiplexer_3_out, multiplexer_4_out, xor_1_out, xor_2_out;

  xor xor_1 (xor_1_out, A, B);
  xor xor_2 (xor_2_out, A, B, C);
  Multiplexer multiplexer_1 (.in0(_0), .in1(B), .out(multiplexer_1_out), .sel(A), .en(Enable));
  Multiplexer multiplexer_2 (.in0(B), .in1(_1), .out(multiplexer_2_out), .sel(A), .en(Enable));
  Multiplexer multiplexer_3 (.in0(B), .in1(_0_2), .out(multiplexer_3_out), .sel(A), .en(Enable));
  Multiplexer multiplexer_4 (.in0(_1_2), .in1(B), .out(multiplexer_4_out), .sel(A), .en(Enable));
  Multiplexer #(.select(3)) multiplexer_5 (
    .in0(multiplexer_1_out), .in1(multiplexer_1_out), .in2(multiplexer_3_out), .in3(multiplexer_3_out),
    .in4(multiplexer_1_out), .in5(multiplexer_2_out), .in6(multiplexer_3_out), .in7(multiplexer_4_out),
    .out(Y1), .sel({F1, F0, C}), .en(F2));
  Multiplexer #(.select(3)) multiplexer_6 (
    .in0(in_2), .in1(multiplexer_2_out), .in2(multiplexer_1_out), .in3(xor_1_out), .in4(xor_1_out),
    .in5(xor_1_out), .in6(xor_2_out), .in7(xor_2_out), .out(Y0), .sel({F2, F1, F0}));  // open: en

  // Notes on the sheet:
  //   A.B
  //   A+B
  //   A'.B
  //   A'+B
  //   A(XOR)B
  //   1-bit ALU Circuit
  //   A(XOR)B(XOR)C
endmodule
