// Logisim project AND Gate.circ as structural Verilog
module AND_Gate (
  input  A,
  input  B,
  output C
);

  wire nand_1_out;

  nand nand_1 (nand_1_out, A, B);
  nand nand_2 (C, nand_1_out, nand_1_out);
endmodule
