// Logisim project Asynchronous 3-bit DOWN Counter JK lipflop.circ as structural Verilog: 1 circuit, main circuit main
module main (
  input  in_1,
  output Q0,
  output Q1,
  output Q2
);

  wire clock_1_out;

  Clock clock_1 (.out(clock_1_out));
  J_K_Flip_Flop j_k_ff_1 (.J(in_1), .clk(clock_1_out), .K(in_1), .Q(Q0));  // open: Qn, preset, en, reset
  J_K_Flip_Flop j_k_ff_2 (.J(in_1), .clk(Q0), .K(in_1), .Q(Q1));  // open: Qn, preset, en, reset
  J_K_Flip_Flop j_k_ff_3 (.J(in_1), .clk(Q1), .K(in_1), .Q(Q2));  // open: Qn, preset, en, reset

  // Notes on the sheet:
  //   Clock
  //   Asynchronous 3-bit DOWN Counter
endmodule
