// Logisim project BCD to Excess-3.circ as structural Verilog: 1 circuit, main circuit main
module main (
  input  [3:0] BCD,
  output [3:0] Excess_3
);

  wire and_1_out, or_1_out;

  or or_1 (or_1_out, BCD[0], BCD[1]);
  xnor xnor_1 (Excess_3[1], BCD[1], BCD[0]);
  not not_1 (Excess_3[0], BCD[0]);
  and and_1 (and_1_out, or_1_out, BCD[2]);
  xor xor_1 (Excess_3[2], or_1_out, BCD[2]);
  or or_2 (Excess_3[3], and_1_out, BCD[3]);

  // Notes on the sheet:
  //   BCD to Excess-3 Circuit
endmodule
