// Logisim project BCD to Gray Code.circ as structural Verilog: 2 circuits, main circuit main
module main (
  input  [3:0] Binary,
  output [3:0] Gray
);

  xor xor_1 (Gray[2], Binary[3], Binary[2]);
  xor xor_2 (Gray[1], Binary[2], Binary[1]);
  xor xor_3 (Gray[0], Binary[1], Binary[0]);

  assign Gray[3] = Binary[3];

  // Notes on the sheet:
  //   BCD Number to Gray Code
endmodule

module Binary_to_Gray (
  input  B3,
  input  B2,
  input  B1,
  input  B0,
  output G3,
  output G2,
  output G1,
  output G0
);

  wire and_1_out, and_2_out, and_3_out, and_4_out, and_5_out, and_6_out, not_1_out, not_2_out, not_3_out,
       not_4_out, not_5_out, not_6_out;

  not not_1 (not_1_out, B3);
  and and_1 (and_1_out, not_1_out, B2);
  and and_2 (and_2_out, B3, not_2_out);
  not not_2 (not_2_out, B2);
  not not_3 (not_3_out, B2);
  and and_3 (and_3_out, not_3_out, B1);
  and and_4 (and_4_out, B2, not_4_out);
  not not_4 (not_4_out, B1);
  not not_5 (not_5_out, B1);
  and and_5 (and_5_out, not_5_out, B0);
  and and_6 (and_6_out, B1, not_6_out);
  not not_6 (not_6_out, B0);
  or or_1 (G2, and_1_out, and_2_out);
  or or_2 (G1, and_3_out, and_4_out);
  or or_3 (G0, and_5_out, and_6_out);

  assign G3 = B3;
endmodule
