// Logisim project Decoder.circ as structural Verilog
module Decoder (
  input  x,
  input  y,
  input  z
);

  wire and_1_out, and_2_out, and_3_out, and_4_out, and_5_out, and_6_out, and_7_out, and_8_out, not_1_out,
       not_2_out, not_3_out;

  not not_1 (not_1_out, x);
  not not_2 (not_2_out, y);
  not not_3 (not_3_out, z);
  and and_1 (and_1_out, not_1_out, not_2_out, not_3_out);
  LED led_1 (.in(and_1_out));
  and and_2 (and_2_out, not_1_out, not_2_out, z);
  LED led_2 (.in(and_2_out));
  and and_3 (and_3_out, not_1_out, y, not_3_out);
  LED led_3 (.in(and_3_out));
  and and_4 (and_4_out, not_1_out, y, z);
  LED led_4 (.in(and_4_out));
  LED led_5 (.in(and_5_out));
  and and_5 (and_5_out, x, not_2_out, not_3_out);
  LED led_6 (.in(and_6_out));
  and and_6 (and_6_out, x, not_2_out, z);
  and and_7 (and_7_out, x, y, not_3_out);
  LED led_7 (.in(and_7_out));
  LED led_8 (.in(and_8_out));
  and and_8 (and_8_out, x, y, z);

  // Notes on the sheet:
  //   3 to 8 Decoder  Circuit
  //   D5
  //   D0
  //   D1
  //   D2
  //   D3
  //   D4
  //   D6
  //   D7
endmodule
