// Logisim project Encoder.circ as structural Verilog: 1 circuit, main circuit main
module main (
  input  D0,
  input  D1,
  input  D2,
  input  D3,
  input  D4,
  input  D5,
  input  D6,
  input  D7,
  output X,
  output Y,
  output Z
);

  or or_1 (X, D4, D5, D6, D7);
  or or_2 (Y, D2, D3, D6, D7);
  or or_3 (Z, D1, D3, D5, D7);

  // Notes on the sheet:
  //   Encoder Circuit
  //   D2+D3+D6+D7
  //   D1+D3+D5+D7
  //   D4+D5+D6+D7
endmodule
