// Logisim project Full Adder.circ as structural Verilog
module Full_Adder (
  input  A,
  input  B,
  input  Cin,
  output Sum,
  output Carry
);

  wire nand_1_out, nand_2_out, nand_3_out, nand_4_out, nand_5_out, nand_6_out, nand_7_out, nand_8_out,
       nand_9_out, nand_10_out, nand_11_out, nand_12_out, nand_13_out;

  nand nand_1 (nand_1_out, A, A);
  nand nand_2 (nand_2_out, B, B);
  nand nand_3 (nand_3_out, A, A);
  nand nand_4 (nand_4_out, Cin, Cin);
  nand nand_5 (nand_5_out, B, B);
  nand nand_6 (nand_6_out, Cin, Cin);
  nand nand_7 (nand_7_out, B, Cin);
  nand nand_8 (nand_8_out, A, Cin);
  nand nand_9 (nand_9_out, A, B);
  nand nand_10 (nand_10_out, nand_1_out, nand_2_out, Cin);
  nand nand_11 (nand_11_out, nand_3_out, B, nand_4_out);
  nand nand_12 (nand_12_out, A, nand_5_out, nand_6_out);
  nand nand_13 (nand_13_out, A, B, Cin);
  nand nand_14 (Carry, nand_7_out, nand_8_out, nand_9_out);
  nand nand_15 (Sum, nand_10_out, nand_11_out, nand_12_out, nand_13_out);
endmodule
