// Logisim project Full Subtractor.circ as structural Verilog
module Full_Subtractor (
  input  A,
  input  B,
  input  C,
  output Difference,
  output Borrow
);

  wire nand_1_out, nand_2_out, nand_3_out, nand_4_out, nand_5_out, nand_6_out, nand_7_out, nand_8_out,
       nand_9_out, nand_10_out, nand_11_out, nand_12_out, nand_13_out, nand_14_out, nand_15_out;

  nand nand_1 (nand_1_out, A, A);
  nand nand_2 (nand_2_out, B, B);
  nand nand_3 (nand_3_out, A, A);
  nand nand_4 (nand_4_out, C, C);
  nand nand_5 (nand_5_out, B, B);
  nand nand_6 (nand_6_out, C, C);
  nand nand_7 (nand_7_out, A, A);
  nand nand_8 (nand_8_out, A, A);
  nand nand_9 (nand_9_out, nand_1_out, nand_2_out, C);
  nand nand_10 (nand_10_out, nand_3_out, B, nand_4_out);
  nand nand_11 (nand_11_out, A, nand_5_out, nand_6_out);
  nand nand_12 (nand_12_out, A, B, C);
  nand nand_13 (nand_13_out, nand_7_out, C);
  nand nand_14 (nand_14_out, nand_8_out, B);
  nand nand_15 (nand_15_out, B, C);
  nand nand_16 (Difference, nand_9_out, nand_10_out, nand_11_out, nand_12_out);
  nand nand_17 (Borrow, nand_13_out, nand_14_out, nand_15_out);
endmodule
