// Logisim project Full_Adder.circ as structural Verilog
module main (
  input  C_in,
  input  [3:0] A,
  input  [3:0] B,
  output [3:0] Sum,
  output Carry
);

  wire adder_1_carry, adder_2_carry, adder_3_carry;

  ADDER adder_1 (.A(A[0]), .B(B[0]), .Cin(C_in), .Sum(Sum[0]), .Carry(adder_1_carry));
  ADDER adder_2 (.A(A[1]), .B(B[1]), .Cin(adder_1_carry), .Sum(Sum[1]), .Carry(adder_2_carry));
  ADDER adder_3 (.A(A[2]), .B(B[2]), .Cin(adder_2_carry), .Sum(Sum[2]), .Carry(adder_3_carry));
  ADDER adder_4 (.A(A[3]), .B(B[3]), .Cin(adder_3_carry), .Sum(Sum[3]), .Carry(Carry));

  // Notes on the sheet:
  //   4-Bit Adder
endmodule

module ADDER (
  input  A,
  input  B,
  input  Cin,
  output Sum,
  output Carry
);

  wire nand_1_out, nand_2_out, nand_3_out, nand_4_out, nand_5_out, nand_6_out, nand_7_out, nand_8_out,
       nand_9_out, nand_10_out, nand_11_out, nand_12_out, nand_13_out;

  nand nand_1 (nand_1_out, A, A);
  nand nand_2 (nand_2_out, B, B);
  nand nand_3 (nand_3_out, A, A);
  nand nand_4 (nand_4_out, Cin, Cin);
  nand nand_5 (nand_5_out, B, B);
  nand nand_6 (nand_6_out, Cin, Cin);
  nand nand_7 (nand_7_out, B, Cin);
  nand nand_8 (nand_8_out, A, Cin);
  nand nand_9 (nand_9_out, A, B);
  nand nand_10 (nand_10_out, nand_1_out, nand_2_out, Cin);
  nand nand_11 (nand_11_out, nand_3_out, B, nand_4_out);
  nand nand_12 (nand_12_out, A, nand_5_out, nand_6_out);
  nand nand_13 (nand_13_out, A, B, Cin);
  nand nand_14 (Carry, nand_7_out, nand_8_out, nand_9_out);
  nand nand_15 (Sum, nand_10_out, nand_11_out, nand_12_out, nand_13_out);

  // Notes on the sheet:
  //   Full Adder Circuit
endmodule

module _4_Bit_Adder (
  input  C_in,
  input  [3:0] A4_0to3,
  input  [3:0] B4_0to3,
  input  [3:0] A4_4to7,
  input  [3:0] B4_4to7,
  output [3:0] S4_0to3,
  output [3:0] S4_4to7,
  output C_out
);

  wire main_1_carry;

  main main_1 (.C_in(C_in), .A(A4_0to3), .B(B4_0to3), .Sum(S4_0to3), .Carry(main_1_carry));
  main main_2 (.C_in(main_1_carry), .A(A4_4to7), .B(B4_4to7), .Sum(S4_4to7), .Carry(C_out));

  // Notes on the sheet:
  //   8-Bit Adder
endmodule

module _8_Bit_Adder (
  input  C_in,
  input  [3:0] A_0to3,
  input  [3:0] B_0to3,
  input  [3:0] A_4to7,
  input  [3:0] B_4to7,
  input  [3:0] A_8to11,
  input  [3:0] B_8to11,
  input  [3:0] A_12to15,
  input  [3:0] B_12to15,
  output [3:0] S_0to3,
  output [3:0] S_4to7,
  output [3:0] S_8to11,
  output [3:0] S_12to15,
  output out_14
);

  wire main_1_carry, main_2_carry, main_3_carry;

  main main_1 (.C_in(C_in), .A(A_0to3), .B(B_0to3), .Sum(S_0to3), .Carry(main_1_carry));
  main main_2 (.C_in(main_1_carry), .A(A_4to7), .B(B_4to7), .Sum(S_4to7), .Carry(main_2_carry));
  main main_3 (.C_in(main_2_carry), .A(A_8to11), .B(B_8to11), .Sum(S_8to11), .Carry(main_3_carry));
  main main_4 (.C_in(main_3_carry), .A(A_12to15), .B(B_12to15), .Sum(S_12to15), .Carry(out_14));

  // Notes on the sheet:
  //   16-Bit Adder
endmodule
