// Logisim project Full_Subtractor.circ as structural Verilog
module main (
  input  C_in,
  input  [3:0] A_0to3,
  input  [3:0] B_0to3,
  input  [3:0] A_4to7,
  input  [3:0] B_4to7,
  input  [3:0] A_8to11,
  input  [3:0] B_8to11,
  input  [3:0] A_12to15,
  input  [3:0] B_12to15,
  output [3:0] D_0to3,
  output [3:0] D_4to7,
  output [3:0] D_8to11,
  output [3:0] D_12to15,
  output Borrow
);

  wire full_subtractor_1_borrow, full_subtractor_2_borrow, full_subtractor_3_borrow;

  Full_Subtractor full_subtractor_1 (
    .C_in(C_in), .A(A_0to3), .B(B_0to3), .Difference(D_0to3), .Borrow(full_subtractor_1_borrow));
  Full_Subtractor full_subtractor_2 (
    .C_in(full_subtractor_1_borrow), .A(A_4to7), .B(B_4to7), .Difference(D_4to7),
    .Borrow(full_subtractor_2_borrow));
  Full_Subtractor full_subtractor_3 (
    .C_in(full_subtractor_2_borrow), .A(A_8to11), .B(B_8to11), .Difference(D_8to11),
    .Borrow(full_subtractor_3_borrow));
  Full_Subtractor full_subtractor_4 (
    .C_in(full_subtractor_3_borrow), .A(A_12to15), .B(B_12to15), .Difference(D_12to15), .Borrow(Borrow));

  // Notes on the sheet:
  //   16-Bit Subtractor
endmodule

module Subtractor (
  input  A,
  input  B,
  input  Cin,
  output Difference,
  output Borrow
);

  wire and_1_out, and_2_out, and_3_out, and_4_out, and_5_out, and_6_out, and_7_out, and_8_out, and_9_out,
       and_10_out, and_11_out, not_1_out, not_2_out, not_3_out, not_4_out, not_5_out, not_6_out, not_7_out,
       not_8_out, or_1_out, or_2_out, or_3_out;

  not not_1 (not_1_out, A);
  not not_2 (not_2_out, B);
  not not_3 (not_3_out, A);
  not not_4 (not_4_out, B);
  not not_5 (not_5_out, A);
  not not_6 (not_6_out, A);
  and and_1 (and_1_out, not_1_out, not_2_out);
  and and_2 (and_2_out, not_3_out, B);
  not not_7 (not_7_out, Cin);
  and and_3 (and_3_out, A, not_4_out);
  not not_8 (not_8_out, Cin);
  and and_4 (and_4_out, A, B);
  and and_5 (and_5_out, not_5_out, Cin);
  and and_6 (and_6_out, not_6_out, B);
  and and_7 (and_7_out, and_1_out, Cin);
  and and_8 (and_8_out, and_2_out, not_7_out);
  and and_9 (and_9_out, and_3_out, not_8_out);
  and and_10 (and_10_out, and_4_out, Cin);
  or or_1 (or_1_out, and_5_out, and_6_out);
  and and_11 (and_11_out, B, Cin);
  or or_2 (or_2_out, and_7_out, and_8_out);
  or or_3 (or_3_out, and_9_out, and_10_out);
  or or_4 (Borrow, or_1_out, and_11_out);
  or or_5 (Difference, or_2_out, or_3_out);

  // Notes on the sheet:
  //   Full Subtractor Circuit
endmodule

module Full_Subtractor (
  input  C_in,
  input  [3:0] A,
  input  [3:0] B,
  output [3:0] Difference,
  output Borrow
);

  wire subtractor_1_borrow, subtractor_2_borrow, subtractor_3_borrow;

  Subtractor subtractor_1 (.A(A[0]), .B(B[0]), .Cin(C_in), .Difference(Difference[0]), .Borrow(subtractor_1_borrow));
  Subtractor subtractor_2 (
    .A(A[1]), .B(B[1]), .Cin(subtractor_1_borrow), .Difference(Difference[1]), .Borrow(subtractor_2_borrow));
  Subtractor subtractor_3 (
    .A(A[2]), .B(B[2]), .Cin(subtractor_2_borrow), .Difference(Difference[2]), .Borrow(subtractor_3_borrow));
  Subtractor subtractor_4 (.A(A[3]), .B(B[3]), .Cin(subtractor_3_borrow), .Difference(Difference[3]), .Borrow(Borrow));

  // Notes on the sheet:
  //   4-Bit Subtractor
endmodule

module _16_Bit_Subtractor (
  input  C_in,
  input  [3:0] A_0to3,
  input  [3:0] B_0to3,
  input  [3:0] A_4to7,
  input  [3:0] B_4to7,
  output [3:0] D_0to3,
  output [3:0] D_4to7,
  output Borrow
);

  wire full_subtractor_1_borrow;

  Full_Subtractor full_subtractor_1 (
    .C_in(C_in), .A(A_0to3), .B(B_0to3), .Difference(D_0to3), .Borrow(full_subtractor_1_borrow));
  Full_Subtractor full_subtractor_2 (
    .C_in(full_subtractor_1_borrow), .A(A_4to7), .B(B_4to7), .Difference(D_4to7), .Borrow(Borrow));

  // Notes on the sheet:
  //   8-Bit Subtractor
endmodule
