// Logisim project Gray Code to Binary.circ as structural Verilog: 2 circuits, main circuit main
module main (
  input  [3:0] Gray,
  output [3:0] Binary
);

  xor xor_1 (Binary[2], Gray[3], Gray[2]);
  xor xor_2 (Binary[1], Binary[2], Gray[1]);
  xor xor_3 (Binary[0], Binary[1], Gray[0]);

  assign Binary[3] = Gray[3];

  // Notes on the sheet:
  //   Gray Code To Binary
endmodule

module Gray_to_Binary (
  input  G3,
  input  G2,
  input  G1,
  input  G0,
  output B3,
  output B2,
  output B1,
  output B0
);

  wire and_1_out, and_2_out, and_3_out, and_4_out, and_5_out, and_6_out, and_7_out, and_8_out, and_9_out,
       and_10_out, and_11_out, and_12_out, and_13_out, and_14_out, and_15_out, and_16_out, and_17_out,
       and_18_out, and_19_out, and_20_out, and_21_out, and_22_out, and_23_out, and_24_out, and_25_out,
       and_26_out, and_27_out, and_28_out, and_29_out, and_30_out, and_31_out, and_32_out, and_33_out,
       and_34_out, not_1_out, not_2_out, not_3_out, not_4_out, not_5_out, not_6_out, not_7_out, not_8_out,
       not_9_out, not_10_out, not_11_out, not_12_out, not_13_out, not_14_out, not_15_out, not_16_out,
       not_17_out, not_18_out, not_19_out, not_20_out, not_21_out, not_22_out, not_23_out, not_24_out,
       or_2_out, or_3_out, or_4_out, or_5_out, or_6_out, or_7_out, or_9_out, or_10_out;

  not not_1 (not_1_out, G3);
  and and_1 (and_1_out, not_1_out, G2);
  and and_2 (and_2_out, G3, not_2_out);
  not not_2 (not_2_out, G2);
  not not_3 (not_3_out, G3);
  and and_3 (and_3_out, not_3_out, not_4_out);
  not not_4 (not_4_out, G2);
  not not_5 (not_5_out, G3);
  and and_4 (and_4_out, not_5_out, G2);
  not not_6 (not_6_out, G1);
  and and_5 (and_5_out, G3, not_7_out);
  not not_7 (not_7_out, G2);
  not not_8 (not_8_out, G1);
  and and_6 (and_6_out, G3, G2);
  not not_9 (not_9_out, G3);
  and and_7 (and_7_out, not_9_out, not_10_out);
  not not_10 (not_10_out, G2);
  not not_11 (not_11_out, G1);
  and and_8 (and_8_out, not_11_out, G0);
  not not_12 (not_12_out, G3);
  and and_9 (and_9_out, not_12_out, not_13_out);
  not not_13 (not_13_out, G2);
  and and_10 (and_10_out, G1, not_14_out);
  not not_14 (not_14_out, G0);
  not not_15 (not_15_out, G3);
  and and_11 (and_11_out, not_15_out, G2);
  not not_16 (not_16_out, G1);
  and and_12 (and_12_out, not_16_out, not_17_out);
  not not_17 (not_17_out, G0);
  not not_18 (not_18_out, G3);
  and and_13 (and_13_out, not_18_out, G2);
  and and_14 (and_14_out, G1, G0);
  and and_15 (and_15_out, G3, not_19_out);
  not not_19 (not_19_out, G2);
  not not_20 (not_20_out, G1);
  and and_16 (and_16_out, not_20_out, not_21_out);
  not not_21 (not_21_out, G0);
  and and_17 (and_17_out, G3, not_22_out);
  not not_22 (not_22_out, G2);
  and and_18 (and_18_out, G1, G0);
  and and_19 (and_19_out, G3, G2);
  not not_23 (not_23_out, G1);
  and and_20 (and_20_out, not_23_out, G0);
  and and_21 (and_21_out, G3, G2);
  and and_22 (and_22_out, G1, not_24_out);
  not not_24 (not_24_out, G0);
  or or_1 (B2, and_1_out, and_2_out);
  and and_23 (and_23_out, and_3_out, G1);
  and and_24 (and_24_out, and_4_out, not_6_out);
  and and_25 (and_25_out, and_5_out, not_8_out);
  and and_26 (and_26_out, and_6_out, G1);
  and and_27 (and_27_out, and_7_out, and_8_out);
  and and_28 (and_28_out, and_9_out, and_10_out);
  and and_29 (and_29_out, and_11_out, and_12_out);
  and and_30 (and_30_out, and_13_out, and_14_out);
  and and_31 (and_31_out, and_15_out, and_16_out);
  and and_32 (and_32_out, and_17_out, and_18_out);
  and and_33 (and_33_out, and_19_out, and_20_out);
  and and_34 (and_34_out, and_21_out, and_22_out);
  or or_2 (or_2_out, and_23_out, and_24_out);
  or or_3 (or_3_out, and_25_out, and_26_out);
  or or_4 (or_4_out, and_27_out, and_28_out);
  or or_5 (or_5_out, and_29_out, and_30_out);
  or or_6 (or_6_out, and_31_out, and_32_out);
  or or_7 (or_7_out, and_33_out, and_34_out);
  or or_8 (B1, or_2_out, or_3_out);
  or or_9 (or_9_out, or_4_out, or_5_out);
  or or_10 (or_10_out, or_6_out, or_7_out);
  or or_11 (B0, or_9_out, or_10_out);

  assign B3 = G3;
endmodule
