// Logisim project Half Adder.circ as structural Verilog
module Half_Adder (
  input  A,
  input  B,
  output Sum,
  output Carry
);

  wire nand_1_out, nand_2_out, nand_3_out, nand_4_out, nand_5_out;

  nand nand_1 (nand_1_out, A, A);
  nand nand_2 (nand_2_out, B, B);
  nand nand_3 (nand_3_out, A, B);
  nand nand_4 (nand_4_out, nand_1_out, B);
  nand nand_5 (nand_5_out, A, nand_2_out);
  nand nand_6 (Carry, nand_3_out, nand_3_out);
  nand nand_7 (Sum, nand_4_out, nand_5_out);
endmodule
