// Logisim project Half Subtractor.circ as structural Verilog
module Half_Subtractor (
  input  A,
  input  B,
  output Diff,
  output Carry
);

  wire nand_1_out, nand_2_out, nand_3_out, nand_4_out, nand_5_out, nand_6_out;

  nand nand_1 (nand_1_out, A, A);
  nand nand_2 (nand_2_out, B, B);
  nand nand_3 (nand_3_out, A, A);
  nand nand_4 (nand_4_out, nand_1_out, B);
  nand nand_5 (nand_5_out, A, nand_2_out);
  nand nand_6 (nand_6_out, nand_3_out, B);
  nand nand_7 (Diff, nand_4_out, nand_5_out);
  nand nand_8 (Carry, nand_6_out, nand_6_out);
endmodule
