// Logisim project JK Latch.circ as structural Verilog: 1 circuit, main circuit main
module main (
  input  K,
  input  Enable,
  input  J,
  output Q,
  output Q_prime
);

  wire and_1_out, and_2_out;

  and and_1 (and_1_out, Q, K, Enable);
  and and_2 (and_2_out, Enable, J, Q_prime);
  nor nor_1 (Q, and_1_out, Q_prime);
  nor nor_2 (Q_prime, Q, and_2_out);

  // Notes on the sheet:
  //   JK Latch
endmodule
