// Logisim project Multiplier Circuit.circ as structural Verilog: 1 circuit, main circuit main
module main (
  input  A1,
  input  A0,
  input  B1,
  input  B0,
  output P0,
  output P1,
  output P2,
  output P3
);

  wire and_2_out, and_3_out, and_4_out, and_5_out;

  and and_1 (P0, A0, B0);
  and and_2 (and_2_out, A1, B0);
  and and_3 (and_3_out, A0, B1);
  and and_4 (and_4_out, A1, B1);
  xor xor_1 (P1, and_2_out, and_3_out);
  and and_5 (and_5_out, and_2_out, and_3_out);
  xor xor_2 (P2, and_5_out, and_4_out);
  and and_6 (P3, and_5_out, and_4_out);

  // Notes on the sheet:
  //   Multiplier Circuit
endmodule
