// Logisim project NOR Gate.circ as structural Verilog
module NOR_Gate (
  input  A,
  input  B,
  output C
);

  wire nand_1_out, nand_2_out, nand_3_out;

  nand nand_1 (nand_1_out, A, A);
  nand nand_2 (nand_2_out, B, B);
  nand nand_3 (nand_3_out, nand_1_out, nand_2_out);
  nand nand_4 (C, nand_3_out, nand_3_out);
endmodule
