// Logisim project OR Gate.circ as structural Verilog
module OR_Gate (
  input  A,
  input  B,
  output C
);

  wire nand_1_out, nand_2_out;

  nand nand_1 (nand_1_out, B, B);
  nand nand_2 (nand_2_out, A, A);
  nand nand_3 (C, nand_1_out, nand_2_out);
endmodule
