// Logisim project Universal Shift Register.circ as structural Verilog: 1 circuit, main circuit main
module main (
  input  Reset,
  input  [1:0] S,
  input  Shift_Left,
  input  Shift_Right,
  input  in_5,
  input  in_6,
  input  in_7,
  input  in_8,
  output A3,
  output A2,
  output A1,
  output A0
);

  wire clock_1_out, multiplexer_1_out, multiplexer_2_out, multiplexer_3_out, multiplexer_4_out;

  Clock clock_1 (.out(clock_1_out));
  D_Flip_Flop d_ff_1 (.D(multiplexer_1_out), .clk(clock_1_out), .Q(A3), .reset(Reset));  // open: Qn, preset
  Multiplexer #(.enable("false"), .select(2)) multiplexer_1 (
    .in0(A3), .in1(Shift_Right), .in2(A2), .in3(in_5), .out(multiplexer_1_out), .sel(S));
  Multiplexer #(.enable("false"), .select(2)) multiplexer_2 (
    .in0(A2), .in1(A3), .in2(A1), .in3(in_6), .out(multiplexer_2_out), .sel(S));
  D_Flip_Flop d_ff_2 (.D(multiplexer_2_out), .clk(clock_1_out), .Q(A2), .reset(Reset));  // open: Qn, preset
  D_Flip_Flop d_ff_3 (.D(multiplexer_3_out), .clk(clock_1_out), .Q(A1), .reset(Reset));  // open: Qn, preset
  Multiplexer #(.enable("false"), .select(2)) multiplexer_3 (
    .in0(A1), .in1(A2), .in2(A0), .in3(in_7), .out(multiplexer_3_out), .sel(S));
  Multiplexer #(.enable("false"), .select(2)) multiplexer_4 (
    .in0(A0), .in1(A1), .in2(Shift_Left), .in3(in_8), .out(multiplexer_4_out), .sel(S));
  D_Flip_Flop d_ff_4 (.D(multiplexer_4_out), .clk(clock_1_out), .Q(A0), .reset(Reset));  // open: Qn, preset

  // Notes on the sheet:
  //   CLK
  //   I3
  //   I2
  //   Universal Shift Register
  //   I1
  //   I0
endmodule
