// Logisim project XOR Gate.circ as structural Verilog
module XOR_Gate (
  input  A,
  input  B,
  output C
);

  wire nand_1_out, nand_2_out, nand_3_out, nand_4_out;

  nand nand_1 (nand_1_out, A, A);
  nand nand_2 (nand_2_out, B, B);
  nand nand_3 (nand_3_out, nand_1_out, B);
  nand nand_4 (nand_4_out, A, nand_2_out);
  nand nand_5 (C, nand_3_out, nand_4_out);
endmodule
